// Logisim project 4bitCpu.circ as structural Verilog: 1 circuit, main circuit main
module main (
);

  wire Add, and_1_out, button_1_out, button_2_out, button_3_out, button_4_out, C0, C1, C2, C3, C4, C5, C6,
       C7, C8, C9, C10, C11, C12, C13, C14, C15, ChangeRomSec, CheckInput, CL, comparator_1_eq,
       controlled_buffer_6_out, controlled_buffer_7_out, controlled_buffer_8_out, controlled_buffer_9_out,
       decoder_1_out0, decoder_1_out1, decoder_1_out2, decoder_1_out3, decoder_1_out4, decoder_1_out5,
       decoder_1_out6, decoder_1_out7, decoder_1_out8, decoder_1_out9, decoder_1_out10, decoder_1_out11,
       decoder_1_out12, decoder_1_out13, decoder_1_out14, decoder_1_out15, decoder_2_out0, decoder_2_out13,
       decoder_2_out14, decoder_2_out15, decoder_4_out0, decoder_4_out1, decoder_4_out2, decoder_4_out3,
       GPUclock, JMP, JMPifA0, LDI, LoadRamBank, LoadRamIntoAFromAdrr, MOV, multiplexer_1_out, or_1_out,
       or_2_out, register_3_q, register_4_q, register_5_q, register_6_q, register_7_q, Sub, VramOut,
       writeAintoRamAtAdrr, WriteVRam;
  wire [3:0] adder_1_out, Addout, bit_extender_1_out, controlled_buffer_1_out, InputOut, Operand, outA, outB,
       RamBankAdr, RamOut, register_1_q, register_2_q, RomSec, SubOut, subtractor_1_out;
  wire [7:0] counter_1_q, counter_2_q, rom_1_data;
  wire [7:4] register_8_q;
  wire [15:0] controlled_buffer_10_out, controlled_buffer_12_out, controlled_buffer_14_out,
       controlled_buffer_16_out, controlled_buffer_18_out, controlled_buffer_20_out,
       controlled_buffer_22_out, controlled_buffer_24_out, controlled_buffer_26_out,
       controlled_buffer_28_out, controlled_buffer_30_out, controlled_buffer_32_out,
       controlled_buffer_34_out, controlled_buffer_36_out, controlled_buffer_37_out,
       controlled_buffer_38_out, Row0out, Row1out, Row2out, Row3out, Row4out, Row5out, Row6out, Row7out,
       Row8out, Row9out, Row10out, Row11out, Row12out, Row13out, Row14out, Row15out;

  Comparator #(.width(4)) comparator_1 (.a(outA), .b(4'b0000), .eq(comparator_1_eq));  // open: gt, lt
  Register #(.width(4)) register_1 (.Q(register_1_q));  // open: D, en, clk, clr
  Register #(.width(4)) register_2 (.Q(register_2_q));  // open: D, en, clk, clr
  and and_1 (and_1_out, JMPifA0, comparator_1_eq);
  or or_1 (or_1_out, and_1_out, JMP);
  Clock #(.highDuration(5), .lowDuration(5)) clock_1 (.out(CL));
  Clock clock_2 (.out(GPUclock));
  Counter counter_1 (
    .clr(1'b0), .load(or_1_out), .up(1'b1), .clk(CL), .D({RomSec, Operand}), .Q(counter_1_q));  // open: count, carry
  Counter counter_2 (
    .load(WriteVRam), .up(1'b1), .clk(GPUclock), .D({register_2_q, register_1_q}), .Q(counter_2_q));  // open: clr, count, carry
  Register #(.width(1)) register_3 (.D(WriteVRam), .en(1'b1), .clk(GPUclock), .Q(register_3_q));  // open: clr
  Register #(.width(1)) register_4 (.D(Add), .en(1'b1), .clk(CL), .Q(register_4_q));  // open: clr
  Register #(.width(1)) register_5 (.D(Sub), .en(1'b1), .clk(CL), .Q(register_5_q));  // open: clr
  Register #(.width(1)) register_6 (.D(LoadRamIntoAFromAdrr), .en(1'b1), .clk(CL), .Q(register_6_q));  // open: clr
  Register #(.width(1)) register_7 (.D(CheckInput), .en(1'b1), .clk(CL), .Q(register_7_q));  // open: clr
  RAM #(.dataWidth(4)) GeneralRam (
    .addr({Operand, RamBankAdr}), .we(writeAintoRamAtAdrr), .oe(LoadRamIntoAFromAdrr), .clk(CL), .din(outA),
    .dout(RamOut));
  ROM rom_1 (.addr(counter_1_q), .data(rom_1_data));
  assign controlled_buffer_1_out = register_7_q ? InputOut : 4'bz;  // Controlled_Buffer controlled_buffer_1
  assign controlled_buffer_1_out = register_4_q ? Addout : 4'bz;  // Controlled_Buffer controlled_buffer_2
  assign controlled_buffer_1_out = register_5_q ? SubOut : 4'bz;  // Controlled_Buffer controlled_buffer_3
  assign controlled_buffer_1_out = register_6_q ? RamOut : 4'bz;  // Controlled_Buffer controlled_buffer_4
  assign controlled_buffer_1_out = LDI ? Operand : 4'bz;  // Controlled_Buffer controlled_buffer_5
  RAM #(.dataWidth(1)) VRam (
    .addr(counter_2_q), .we(register_3_q), .oe(1'b1), .clk(GPUclock), .dout(VramOut));  // open: din
  or or_2 (or_2_out, register_4_q, register_5_q, register_7_q, register_6_q, LDI);
  Register register_8 (.D(rom_1_data), .en(1'b1), .clk(CL), .Q({register_8_q, Operand}), .clr(1'b0));
  Register #(.width(4)) B (.D(outA), .en(MOV), .clk(CL), .Q(outB));  // open: clr
  Register #(.width(4)) A (.D(controlled_buffer_1_out), .en(or_2_out), .clk(CL), .Q(outA));  // open: clr
  Register #(.width(4)) RamBankAdress (.D(Operand), .en(LoadRamBank), .clk(CL), .Q(RamBankAdr));  // open: clr
  Register #(.width(4)) u_RomSec (.D(Operand), .en(ChangeRomSec), .clk(CL), .Q(RomSec));  // open: clr
  Decoder #(.select(4)) decoder_1 (
    .out0(decoder_1_out0), .out1(decoder_1_out1), .out2(decoder_1_out2), .out3(decoder_1_out3),
    .out4(decoder_1_out4), .out5(decoder_1_out5), .out6(decoder_1_out6), .out7(decoder_1_out7),
    .out8(decoder_1_out8), .out9(decoder_1_out9), .out10(decoder_1_out10), .out11(decoder_1_out11),
    .out12(decoder_1_out12), .out13(decoder_1_out13), .out14(decoder_1_out14), .out15(decoder_1_out15),
    .sel(counter_2_q[7:4]));  // open: en
  LED led_1 (.in(decoder_2_out0));
  LED led_2 (.in(decoder_2_out13));
  LED led_3 (.in(decoder_2_out14));
  LED led_4 (.in(decoder_2_out15));
  Decoder #(.select(4)) decoder_2 (
    .out0(decoder_2_out0), .out1(LDI), .out2(Add), .out3(Sub), .out4(MOV), .out5(CheckInput), .out6(JMP),
    .out7(JMPifA0), .out8(ChangeRomSec), .out9(LoadRamBank), .out10(writeAintoRamAtAdrr),
    .out11(LoadRamIntoAFromAdrr), .out12(WriteVRam), .out13(decoder_2_out13), .out14(decoder_2_out14),
    .out15(decoder_2_out15), .sel(register_8_q), .en(1'b1));
  Decoder #(.select(4)) decoder_3 (
    .out0(C15), .out1(C14), .out2(C13), .out3(C12), .out4(C11), .out5(C10), .out6(C9), .out7(C8), .out8(C7),
    .out9(C6), .out10(C5), .out11(C4), .out12(C3), .out13(C2), .out14(C1), .out15(C0), .sel(counter_2_q[3:0]));  // open: en
  Adder #(.width(4)) adder_1 (.a(outA), .b(outB), .out(adder_1_out));  // open: cin, cout
  Subtractor #(.width(4)) subtractor_1 (.a(outA), .b(outB), .out(subtractor_1_out));  // open: bin, bout
  Register #(.width(4)) register_9 (.D(adder_1_out), .en(Add), .clk(CL), .Q(Addout));  // open: clr
  Register #(.width(4)) register_10 (.D(subtractor_1_out), .en(Sub), .clk(CL), .Q(SubOut));  // open: clr
  Decoder #(.select(2)) decoder_4 (
    .out0(decoder_4_out0), .out1(decoder_4_out1), .out2(decoder_4_out2), .out3(decoder_4_out3),
    .sel(Operand[1:0]));  // open: en
  Button button_1 (.out(button_1_out));
  Button button_2 (.out(button_2_out));
  Button button_3 (.out(button_3_out));
  assign controlled_buffer_6_out = decoder_4_out2 ? button_2_out : 1'bz;  // Controlled_Buffer controlled_buffer_6
  assign controlled_buffer_7_out = decoder_4_out3 ? button_1_out : 1'bz;  // Controlled_Buffer controlled_buffer_7
  Button button_4 (.out(button_4_out));
  Button button_5 ();  // open: out
  assign controlled_buffer_8_out = decoder_4_out0 ? button_3_out : 1'bz;  // Controlled_Buffer controlled_buffer_8
  assign controlled_buffer_9_out = decoder_4_out1 ? button_4_out : 1'bz;  // Controlled_Buffer controlled_buffer_9
  Multiplexer #(.select(2)) multiplexer_1 (
    .in0(controlled_buffer_8_out), .in1(controlled_buffer_9_out), .in2(controlled_buffer_6_out),
    .in3(controlled_buffer_7_out), .out(multiplexer_1_out), .sel(Operand[1:0]));
  assign bit_extender_1_out = {{3{1'b0}}, multiplexer_1_out};  // Bit_Extender bit_extender_1
  assign controlled_buffer_10_out = decoder_1_out0 ? {C15, C14, C13, C12, C11, C10, C9, C8, C7, C6, C5, C4, C3, C2, C1, C0} : 16'bz;  // Controlled_Buffer controlled_buffer_10
  assign Row0out = VramOut ? controlled_buffer_10_out : 16'bz;  // Controlled_Buffer controlled_buffer_11
  assign controlled_buffer_12_out = decoder_1_out1 ? {C15, C14, C13, C12, C11, C10, C9, C8, C7, C6, C5, C4, C3, C2, C1, C0} : 16'bz;  // Controlled_Buffer controlled_buffer_12
  assign Row1out = VramOut ? controlled_buffer_12_out : 16'bz;  // Controlled_Buffer controlled_buffer_13
  assign controlled_buffer_14_out = decoder_1_out2 ? {C15, C14, C13, C12, C11, C10, C9, C8, C7, C6, C5, C4, C3, C2, C1, C0} : 16'bz;  // Controlled_Buffer controlled_buffer_14
  assign Row2out = VramOut ? controlled_buffer_14_out : 16'bz;  // Controlled_Buffer controlled_buffer_15
  assign controlled_buffer_16_out = decoder_1_out3 ? {C15, C14, C13, C12, C11, C10, C9, C8, C7, C6, C5, C4, C3, C2, C1, C0} : 16'bz;  // Controlled_Buffer controlled_buffer_16
  assign Row3out = VramOut ? controlled_buffer_16_out : 16'bz;  // Controlled_Buffer controlled_buffer_17
  Register #(.width(4)) register_11 (.D(bit_extender_1_out), .en(CheckInput), .clk(CL), .Q(InputOut));  // open: clr
  assign controlled_buffer_18_out = decoder_1_out4 ? {C15, C14, C13, C12, C11, C10, C9, C8, C7, C6, C5, C4, C3, C2, C1, C0} : 16'bz;  // Controlled_Buffer controlled_buffer_18
  assign Row4out = VramOut ? controlled_buffer_18_out : 16'bz;  // Controlled_Buffer controlled_buffer_19
  assign controlled_buffer_20_out = decoder_1_out5 ? {C15, C14, C13, C12, C11, C10, C9, C8, C7, C6, C5, C4, C3, C2, C1, C0} : 16'bz;  // Controlled_Buffer controlled_buffer_20
  assign Row5out = VramOut ? controlled_buffer_20_out : 16'bz;  // Controlled_Buffer controlled_buffer_21
  assign controlled_buffer_22_out = decoder_1_out6 ? {C15, C14, C13, C12, C11, C10, C9, C8, C7, C6, C5, C4, C3, C2, C1, C0} : 16'bz;  // Controlled_Buffer controlled_buffer_22
  assign Row6out = VramOut ? controlled_buffer_22_out : 16'bz;  // Controlled_Buffer controlled_buffer_23
  assign controlled_buffer_24_out = decoder_1_out7 ? {C15, C14, C13, C12, C11, C10, C9, C8, C7, C6, C5, C4, C3, C2, C1, C0} : 16'bz;  // Controlled_Buffer controlled_buffer_24
  assign Row7out = VramOut ? controlled_buffer_24_out : 16'bz;  // Controlled_Buffer controlled_buffer_25
  assign controlled_buffer_26_out = decoder_1_out8 ? {C15, C14, C13, C12, C11, C10, C9, C8, C7, C6, C5, C4, C3, C2, C1, C0} : 16'bz;  // Controlled_Buffer controlled_buffer_26
  assign Row8out = VramOut ? controlled_buffer_26_out : 16'bz;  // Controlled_Buffer controlled_buffer_27
  assign controlled_buffer_28_out = decoder_1_out9 ? {C15, C14, C13, C12, C11, C10, C9, C8, C7, C6, C5, C4, C3, C2, C1, C0} : 16'bz;  // Controlled_Buffer controlled_buffer_28
  assign Row9out = VramOut ? controlled_buffer_28_out : 16'bz;  // Controlled_Buffer controlled_buffer_29
  assign controlled_buffer_30_out = decoder_1_out10 ? {C15, C14, C13, C12, C11, C10, C9, C8, C7, C6, C5, C4, C3, C2, C1, C0} : 16'bz;  // Controlled_Buffer controlled_buffer_30
  assign Row10out = VramOut ? controlled_buffer_30_out : 16'bz;  // Controlled_Buffer controlled_buffer_31
  assign controlled_buffer_32_out = decoder_1_out11 ? {C15, C14, C13, C12, C11, C10, C9, C8, C7, C6, C5, C4, C3, C2, C1, C0} : 16'bz;  // Controlled_Buffer controlled_buffer_32
  assign Row11out = VramOut ? controlled_buffer_32_out : 16'bz;  // Controlled_Buffer controlled_buffer_33
  assign controlled_buffer_34_out = decoder_1_out12 ? {C15, C14, C13, C12, C11, C10, C9, C8, C7, C6, C5, C4, C3, C2, C1, C0} : 16'bz;  // Controlled_Buffer controlled_buffer_34
  assign Row12out = VramOut ? controlled_buffer_34_out : 16'bz;  // Controlled_Buffer controlled_buffer_35
  assign controlled_buffer_36_out = decoder_1_out13 ? {C15, C14, C13, C12, C11, C10, C9, C8, C7, C6, C5, C4, C3, C2, C1, C0} : 16'bz;  // Controlled_Buffer controlled_buffer_36
  assign controlled_buffer_37_out = decoder_1_out14 ? {C15, C14, C13, C12, C11, C10, C9, C8, C7, C6, C5, C4, C3, C2, C1, C0} : 16'bz;  // Controlled_Buffer controlled_buffer_37
  assign controlled_buffer_38_out = decoder_1_out15 ? {C15, C14, C13, C12, C11, C10, C9, C8, C7, C6, C5, C4, C3, C2, C1, C0} : 16'bz;  // Controlled_Buffer controlled_buffer_38
  assign Row13out = VramOut ? controlled_buffer_36_out : 16'bz;  // Controlled_Buffer controlled_buffer_39
  assign Row14out = VramOut ? controlled_buffer_37_out : 16'bz;  // Controlled_Buffer controlled_buffer_40
  assign Row15out = VramOut ? controlled_buffer_38_out : 16'bz;  // Controlled_Buffer controlled_buffer_41
  // LedBar #(.inputtype("row"), .matrixcols(16), .persist(256)) ledbar_1: pin names not known; wires that end beside it: Row0out, Row0out
  // LedBar #(.inputtype("row"), .matrixcols(16), .persist(256)) ledbar_2: pin names not known; wires that end beside it: Row1out, Row1out
  // LedBar #(.inputtype("row"), .matrixcols(16), .persist(256)) ledbar_3: pin names not known; wires that end beside it: Row2out, Row2out
  // LedBar #(.inputtype("row"), .matrixcols(16), .persist(256)) ledbar_4: pin names not known; wires that end beside it: Row3out, Row3out
  // LedBar #(.inputtype("row"), .matrixcols(16), .persist(256)) ledbar_5: pin names not known; wires that end beside it: Row4out, Row4out
  // LedBar #(.inputtype("row"), .matrixcols(16), .persist(256)) ledbar_6: pin names not known; wires that end beside it: Row5out, Row5out
  // LedBar #(.inputtype("row"), .matrixcols(16), .persist(256)) ledbar_7: pin names not known; wires that end beside it: Row6out, Row6out
  // LedBar #(.inputtype("row"), .matrixcols(16), .persist(256)) ledbar_8: pin names not known; wires that end beside it: Row7out, Row7out
  // LedBar #(.inputtype("row"), .matrixcols(16), .persist(256)) ledbar_9: pin names not known; wires that end beside it: Row8out, Row8out
  // LedBar #(.inputtype("row"), .matrixcols(16), .persist(256)) ledbar_10: pin names not known; wires that end beside it: Row9out, Row9out
  // LedBar #(.inputtype("row"), .matrixcols(16), .persist(256)) ledbar_11: pin names not known; wires that end beside it: Row10out, Row10out
  // LedBar #(.inputtype("row"), .matrixcols(16), .persist(256)) ledbar_12: pin names not known; wires that end beside it: Row11out, Row11out
  // LedBar #(.inputtype("row"), .matrixcols(16), .persist(256)) ledbar_13: pin names not known; wires that end beside it: Row12out, Row12out
  // LedBar #(.inputtype("row"), .matrixcols(16), .persist(256)) ledbar_14: pin names not known; wires that end beside it: Row13out, Row13out
  // LedBar #(.inputtype("row"), .matrixcols(16), .persist(256)) ledbar_15: pin names not known; wires that end beside it: Row14out, Row14out
  // LedBar #(.inputtype("row"), .matrixcols(16), .persist(256)) ledbar_16: pin names not known; wires that end beside it: Row15out, Row15out

  // Notes on the sheet:
  //   contents of rom_1 (hex, n*v repeats v):
  //   51 0 40
  //   Opcode
  //   2
  //   3
  //   0
  //   Input
  //   On/Off
  //   1
endmodule
